// Logisim project 02-05.circ as structural Verilog: 1 circuit, main circuit main
module main (
  input  A,
  input  B,
  input  C
);

  wire and_1_out, L1_out, L2_out, L3_out, L5_out, L6_out, L7_out, or_1_out;

  or L1 (L1_out, C, B, A);
  or L2 (L2_out, B, A);
  and and_1 (and_1_out, C, B);
  or L3 (L3_out, and_1_out, A);
  or or_1 (or_1_out, B, C);
  LED led_1 (.in(L1_out));
  LED led_2 (.in(L2_out));
  LED led_3 (.in(L3_out));
  LED led_4 (.in(A));
  and L5 (L5_out, or_1_out, A);
  LED led_5 (.in(L5_out));
  and L6 (L6_out, A, B);
  LED led_6 (.in(L6_out));
  LED led_7 (.in(L7_out));
  and L7 (L7_out, A, B, C);
endmodule
