// Logisim project 21.03.circ as structural Verilog: 2 circuits, main circuit main
module main (
  input  in_1,
  input  in_2,
  input  in_3,
  input  in_4,
  output out_5
);

  S s_1 (.A(in_2), .B(in_1), .C(in_3), .D(in_4), .out_5(out_5));
endmodule

module S (
  input  A,
  input  B,
  input  C,
  input  D,
  output out_5
);

  wire and_1_out, and_2_out, and_3_out, and_4_out, or_1_out, or_2_out;

  or or_1 (or_1_out, D, C);
  and and_1 (and_1_out, A, B);
  or or_2 (or_2_out, A, B);
  and and_2 (and_2_out, or_1_out, and_1_out);
  and and_3 (and_3_out, or_2_out, and_4_out);
  and and_4 (and_4_out, C, D);
  or or_3 (out_5, and_2_out, and_3_out);
endmodule
