// Logisim project 28.03.circ as structural Verilog: 2 circuits, main circuit main
module main (
  input  A,
  input  B,
  input  C,
  input  D,
  output out_5
);

  wire and_1_out, and_2_out;

  or or_1 (out_5, and_1_out, and_2_out);
  and and_1 (and_1_out, A, ~B, C);  // AND_Gate
  and and_2 (and_2_out, B, D);
endmodule

module MACRO (
  input  [3:0] in_1,
  output out_2
);

  main main_1 (.out_5(out_2), .A(in_1[3]), .B(in_1[2]), .C(in_1[1]), .D(in_1[0]));
endmodule
