// Logisim project AULA-DIA-28-02.circ as structural Verilog: 2 circuits, main circuit main
module main (
  input  A,
  input  B,
  input  C,
  input  D,
  output out_5
);

  wire and_1_out, nand_1_out, nor_1_out, nor_2_out, not_1_out, not_2_out, not_3_out, not_4_out, or_1_out,
       xnor_1_out;

  not not_1 (not_1_out, A);
  not not_2 (not_2_out, C);
  not not_3 (not_3_out, D);
  not not_4 (not_4_out, D);
  xnor xnor_1 (xnor_1_out, not_1_out, B);
  and and_1 (and_1_out, not_2_out, not_3_out);
  or or_1 (or_1_out, A, not_4_out);
  nor nor_1 (nor_1_out, B, C);
  nor nor_2 (nor_2_out, xnor_1_out, and_1_out);
  nand nand_1 (nand_1_out, or_1_out, nor_1_out);
  xnor xnor_2 (out_5, nor_2_out, nand_1_out);
endmodule

module TESTE (
  input  [3:0] in_1,
  output out_2
);

  main main_1 (.A(in_1[0]), .B(in_1[1]), .C(in_1[2]), .D(in_1[3]), .out_5(out_2));
endmodule
