// Logisim project Circuitos.circ as structural Verilog: 3 circuits, main circuit main
module main (
  input  A,
  input  B,
  input  VEM_1,
  output S,
  output VAI_1
);

  wire and_1_out, and_2_out, or_1_out, xor_1_out;

  xor xor_1 (xor_1_out, A, B);
  or or_1 (or_1_out, B, VEM_1);
  xor xor_2 (S, xor_1_out, VEM_1);
  and and_1 (and_1_out, or_1_out, A);
  and and_2 (and_2_out, B, VEM_1);
  or or_2 (VAI_1, and_1_out, and_2_out);
endmodule

module Soma (
  input  A,
  input  B,
  input  VEM_1,
  output S,
  output VAI_1
);

  wire and_1_out, and_2_out, or_1_out, xor_1_out;

  xor xor_1 (xor_1_out, A, B);
  or or_1 (or_1_out, B, VEM_1);
  xor xor_2 (S, xor_1_out, VEM_1);
  and and_1 (and_1_out, or_1_out, A);
  and and_2 (and_2_out, B, VEM_1);
  or or_2 (VAI_1, and_1_out, and_2_out);
endmodule

module ADD_4 (
  input  [3:0] in_1,
  input  [3:0] in_2,
  output Overflow,
  output [3:0] out_4
);

  wire soma_2_vai_1, soma_3_vai_1, soma_4_vai_1;

  // Probe on in_2
  Soma soma_1 (.A(in_2[3]), .B(in_1[3]), .VEM_1(soma_2_vai_1), .S(out_4[3]), .VAI_1(Overflow));
  Soma soma_2 (.A(in_2[2]), .B(in_1[2]), .VEM_1(soma_3_vai_1), .S(out_4[2]), .VAI_1(soma_2_vai_1));
  Soma soma_3 (.A(in_2[1]), .B(in_1[1]), .VEM_1(soma_4_vai_1), .S(out_4[1]), .VAI_1(soma_3_vai_1));
  // Probe on out_4
  Soma soma_4 (.A(in_2[0]), .B(in_1[0]), .VEM_1(1'b0), .S(out_4[0]), .VAI_1(soma_4_vai_1));
  // Probe on in_1
endmodule
