// Logisim project aula-07-03.circ as structural Verilog: 1 circuit, main circuit main
module main (
);

  wire and_1_out, and_2_out, and_3_out, and_4_out, and_5_out, and_6_out, and_7_out, and_8_out, clock_1_out,
       or_1_out;
  wire [3:0] counter_1_q, counter_2_q, counter_3_q, counter_4_q, counter_5_q, counter_6_q;

  and and_1 (and_1_out, and_3_out, and_2_out);
  or or_1 (or_1_out, and_1_out, and_5_out);
  and and_2 (and_2_out, ~counter_1_q[0], ~counter_1_q[1], counter_1_q[2], ~counter_1_q[3]);  // AND_Gate
  and and_3 (and_3_out, ~counter_2_q[0], ~counter_2_q[1], counter_2_q[2], ~counter_2_q[3]);  // AND_Gate
  Counter #(.width(4), .max('ha)) counter_1 (
    .Q(counter_1_q), .clk(and_5_out), .clr(and_1_out));  // open: load, D, count, carry
  Counter #(.width(4), .max('ha)) counter_2 (
    .count(and_5_out), .Q(counter_2_q), .clk(and_4_out), .clr(or_1_out));  // open: load, D, carry
  and and_4 (and_4_out, counter_2_q[3], ~counter_2_q[2], counter_2_q[1], ~counter_2_q[0]);  // AND_Gate
  Counter #(.width(4), .max('ha)) counter_3 (
    .Q(counter_3_q), .clk(and_6_out), .clr(and_5_out));  // open: load, D, count, carry
  Counter #(.width(4), .max('ha)) counter_4 (
    .Q(counter_4_q), .clk(and_7_out), .clr(and_6_out));  // open: load, D, count, carry
  and and_5 (and_5_out, ~counter_3_q[3], counter_3_q[2], counter_3_q[1], ~counter_3_q[0]);  // AND_Gate
  and and_6 (and_6_out, counter_4_q[3], ~counter_4_q[2], counter_4_q[1], ~counter_4_q[0]);  // AND_Gate
  Counter #(.width(4), .max('ha)) counter_5 (
    .Q(counter_5_q), .clk(and_8_out), .clr(and_7_out));  // open: load, D, count, carry
  and and_7 (and_7_out, ~counter_5_q[3], counter_5_q[2], counter_5_q[1], ~counter_5_q[0]);  // AND_Gate
  Counter #(.width(4), .max('ha)) counter_6 (
    .Q(counter_6_q), .clk(clock_1_out), .clr(and_8_out));  // open: load, D, count, carry
  and and_8 (and_8_out, counter_6_q[3], ~counter_6_q[2], counter_6_q[1], ~counter_6_q[0]);  // AND_Gate
  Clock clock_1 (.out(clock_1_out));
endmodule
