// Logisim project conversorprojeto.circ as structural Verilog
module a (
  input  A,
  input  B,
  input  C,
  input  D
);

  // OR_Gate or_1 has open pins: in0=A, in1=B, out=open
endmodule

module conversor_projeto (
  input  A,
  input  B,
  input  C,
  input  D,
  input  D_2,
  input  B_2,
  input  C_2,
  input  A_2,
  input  B_3,
  input  C_3,
  input  D_3,
  input  B_4,
  input  C_4,
  input  D_4,
  input  B_5,
  input  C_5,
  input  D_5,
  input  A_3,
  input  B_6,
  input  C_6,
  input  D_6,
  input  A_4,
  input  B_7,
  input  C_7,
  input  D_7
);

  wire and_1_out, and_2_out, and_3_out, and_4_out, and_5_out, and_6_out, and_7_out, or_1_out, or_2_out,
       or_3_out, or_4_out, or_5_out, or_7_out, or_8_out, or_9_out, or_10_out, or_11_out, or_12_out,
       or_13_out, or_14_out, xnor_1_out, xnor_2_out, xor_1_out;

  or or_1 (or_1_out, A_2, B_3);
  xnor xnor_1 (xnor_1_out, B_3, D_3);
  xnor xnor_2 (xnor_2_out, C_4, D_4);
  or or_2 (or_2_out, B_5, ~C_5, D_5);  // OR_Gate
  or or_3 (or_3_out, or_1_out, xnor_1_out);
  or or_4 (or_4_out, ~B_4, xnor_2_out);  // OR_Gate
  or or_5 (or_5_out, A, ~B);  // OR_Gate
  and and_1 (and_1_out, or_5_out, or_8_out);
  or or_6 (or_2_out, and_1_out, or_9_out);
  and and_2 (and_2_out, or_7_out, or_11_out);
  or or_7 (or_7_out, A_3, B_6);
  or or_8 (or_8_out, C, ~D);  // OR_Gate
  and and_3 (and_3_out, B, ~C, D);  // AND_Gate
  or or_9 (or_9_out, and_3_out, and_4_out);
  or or_10 (or_10_out, and_2_out, and_5_out);
  or or_11 (or_11_out, ~C_6, ~D_6);  // OR_Gate
  and and_4 (and_4_out, C, ~D);  // AND_Gate
  _7_Segment_Display u_7_segment_display_1 (
    .g(or_14_out), .f(or_10_out), .a(or_3_out), .b(or_4_out), .e(and_6_out), .d(or_2_out), .c(or_2_out));  // open: dp
  and and_5 (and_5_out, ~C_6, ~D_6);  // AND_Gate
  or or_12 (or_12_out, ~B_2, C_2);  // OR_Gate
  and and_6 (and_6_out, ~D_2, or_12_out);  // AND_Gate
  or or_13 (or_13_out, A_4, xor_1_out);
  or or_14 (or_14_out, or_13_out, and_7_out);
  xor xor_1 (xor_1_out, B_7, C_7);
  and and_7 (and_7_out, C_7, ~D_7);  // AND_Gate

  // Notes on the sheet:
  //   A
  //   B
  //   C
  //   D
  //   F
  //   E
  //   G
endmodule

module conversor (
  input  A,
  input  B,
  input  C,
  input  D
);

  wire and_1_out, and_2_out, and_3_out, and_4_out, and_5_out, and_6_out, and_7_out, not_1_out, or_1_out,
       or_2_out, or_3_out, or_4_out, or_5_out, or_6_out, or_7_out, or_8_out, or_9_out, or_10_out, or_11_out,
       or_12_out, or_13_out, xor_1_out, xor_2_out, xor_3_out;

  xor xor_1 (xor_1_out, B, D);
  xor xor_2 (xor_2_out, C, D);
  or or_1 (or_1_out, B, ~C, D);  // OR_Gate
  or or_2 (or_2_out, C, ~D);  // OR_Gate
  xor xor_3 (xor_3_out, B, C);
  and and_1 (and_1_out, C, ~D);  // AND_Gate
  or or_3 (or_3_out, A, C);
  or or_4 (or_4_out, or_3_out, not_1_out);
  not not_1 (not_1_out, xor_1_out);
  or or_5 (or_5_out, ~B, ~xor_2_out);  // OR_Gate
  or or_6 (or_6_out, A, and_2_out);
  and and_2 (and_2_out, or_2_out, ~B);  // AND_Gate
  and and_3 (and_3_out, B, ~C, D);  // AND_Gate
  and and_4 (and_4_out, C, ~D);  // AND_Gate
  or or_7 (or_7_out, C, ~B);  // OR_Gate
  and and_5 (and_5_out, or_7_out, ~D);  // AND_Gate
  or or_8 (or_8_out, A, B);
  and and_6 (and_6_out, or_8_out, or_9_out);
  or or_9 (or_9_out, ~C, ~D);  // OR_Gate
  and and_7 (and_7_out, ~C, ~D);  // AND_Gate
  or or_10 (or_10_out, A, xor_3_out, and_1_out);
  or or_11 (or_11_out, or_6_out, and_3_out);
  or or_12 (or_12_out, and_6_out, and_7_out);
  or or_13 (or_13_out, or_11_out, and_4_out);
  _7_Segment_Display u_7_segment_display_1 (
    .g(or_10_out), .f(or_12_out), .a(or_4_out), .b(or_5_out), .e(and_5_out), .d(or_13_out), .c(or_1_out));  // open: dp
endmodule
