// Logisim project mion.circ as structural Verilog: 2 circuits, main circuit main
module main (
  input  in_1,
  input  in_2,
  input  in_3,
  input  in_4,
  output out_5
);

  mion mion_1 (.A(in_1), .B(in_2), .C(in_3), .D(in_4), .out_5(out_5));
endmodule

module mion (
  input  A,
  input  B,
  input  C,
  input  D,
  output out_5
);

  wire and_1_out, and_2_out, and_3_out, and_4_out, and_5_out;

  and and_1 (and_1_out, ~A, B, C, D);  // AND_Gate
  and and_2 (and_2_out, A, ~B, C, D);  // AND_Gate
  and and_3 (and_3_out, A, B, ~C, D);  // AND_Gate
  and and_4 (and_4_out, A, B, C, ~D);  // AND_Gate
  and and_5 (and_5_out, A, B, C, D);
  or or_1 (out_5, and_1_out, and_2_out, and_3_out, and_4_out, and_5_out);
endmodule
